# Fritzing sketch schema_connection (saved by Fritzing 0.9.3b)

parts:
  Composant1 = Arduino Uno (Rev3) - ICSP
  8x8_LED_Modul_mit_MAX1 = 8x8 LED Modul mit MAX7219 [package=THT]

nets:
  N1: Composant1.D10_PWM/SS, 8x8_LED_Modul_mit_MAX1.CLK_Eingang
  N2: Composant1.D11_PWM/MOSI, 8x8_LED_Modul_mit_MAX1.CS_Eingang
  N3: Composant1.D12/MISO, 8x8_LED_Modul_mit_MAX1.DIN_Eingang
  N4: Composant1.5V, 8x8_LED_Modul_mit_MAX1.VCC_Eingang
  N5: Composant1.GND, 8x8_LED_Modul_mit_MAX1.GND_Eingang
